// Logisim project alu.circ as structural Verilog: 13 circuits, main circuit main
module main (
  input  [31:0] X,
  input  [31:0] Y,
  input  [3:0] Switch,
  output Equal,
  output [31:0] Result
);

  wire [31:0] add_output, and_output, div_output, mulh_output, mult_output, or_output, rem_output,
       sll_output, slt_output, sra_output, srl_output, xor_output;

  add add (.In_1(X), .In_2(Y), .Out(add_output));
  \and  \and  (.In_1(X), .In_2(Y), .Out(and_output));
  \or  \or  (.In_1(X), .In_2(Y), .Out(or_output));
  \xor  \xor  (.In_1(X), .In_2(Y), .Out(xor_output));
  srl srl (.In_1(X), .In_2(Y), .Out(srl_output));
  sra sra (.In_1(X), .In_2(Y), .Out(sra_output));
  sll sll (.In_1(X), .In_2(Y), .Out(sll_output));
  slt slt (.In_1(X), .In_2(Y), .Out(slt_output));
  div div (.In_1(X), .In_2(Y), .Out(div_output));
  rem rem (.In_1(X), .In_2(Y), .Out(rem_output));
  mult mult (.In_1(X), .In_2(Y), .Out(mult_output));
  mulh mulh (.In_1(X), .In_2(Y), .Out(mulh_output));
  Comparator #(.width(32)) comparator_1 (.a(X), .b(Y), .eq(Equal));  // open: gt, lt
  Multiplexer #(.select(4), .width(32)) multiplexer_1 (
    .in0(add_output), .in1(and_output), .in2(or_output), .in3(xor_output), .in4(srl_output),
    .in5(sra_output), .in6(sll_output), .in7(slt_output), .in8(div_output), .in9(rem_output),
    .in10(mult_output), .in11(mulh_output), .out(Result), .sel(Switch));  // open: in12, in13, in14, in15, en

  // Other names for the same wires on the sheet: S[3:0] = Switch

  // Notes on the sheet:
  //   INPUTS to your circuit
  //   DON'T CHANGE THE LOCATIONS OF THE INPUTS AND OUTPUTS!
  //   OUTPUTS from your circuit
endmodule

module add (
  input  [31:0] In_1,
  input  [31:0] In_2,
  output [31:0] Out
);

  Adder #(.width(32)) adder_1 (.a(In_1), .b(In_2), .out(Out));  // open: cin, cout
endmodule

module \and  (
  input  [31:0] In_1,
  input  [31:0] In_2,
  output [31:0] Out
);

  assign Out = In_1 & In_2;  // AND_Gate and_1, 32 bits wide
endmodule

module \or  (
  input  [31:0] In_1,
  input  [31:0] In_2,
  output [31:0] Out
);

  assign Out = In_1 | In_2;  // OR_Gate or_1, 32 bits wide
endmodule

module \xor  (
  input  [31:0] In_1,
  input  [31:0] In_2,
  output [31:0] Out
);

  assign Out = In_1 ^ In_2;  // XOR_Gate xor_1, 32 bits wide
endmodule

module srl (
  input  [31:0] In_1,
  input  [31:0] In_2,
  output [31:0] Out
);

  wire [4:0] bit_extender_1_out;

  Bit_Extender #(.in_width(32), .out_width(5)) bit_extender_1 (.in(In_2), .out(bit_extender_1_out));
  Shifter #(.width(32), .shift("lr")) shifter_1 (.in(In_1), .\dist (bit_extender_1_out), .out(Out));
endmodule

module sra (
  input  [31:0] In_1,
  input  [31:0] In_2,
  output [31:0] Out
);

  wire [4:0] bit_extender_1_out;

  Bit_Extender #(.in_width(32), .out_width(5)) bit_extender_1 (.in(In_2), .out(bit_extender_1_out));
  Shifter #(.width(32), .shift("ar")) shifter_1 (.in(In_1), .\dist (bit_extender_1_out), .out(Out));
endmodule

module sll (
  input  [31:0] In_1,
  input  [31:0] In_2,
  output [31:0] Out
);

  wire [4:0] bit_extender_1_out;

  Bit_Extender #(.in_width(32), .out_width(5)) bit_extender_1 (.in(In_2), .out(bit_extender_1_out));
  Shifter #(.width(32)) shifter_1 (.in(In_1), .\dist (bit_extender_1_out), .out(Out));
endmodule

module slt (
  input  [31:0] In_1,
  input  [31:0] In_2,
  output [31:0] Out
);

  wire comparator_1_lt;

  Comparator #(.width(32)) comparator_1 (.a(In_1), .b(In_2), .lt(comparator_1_lt));  // open: gt, eq
  assign Out = {{31{1'b0}}, comparator_1_lt};  // Bit_Extender bit_extender_1
endmodule

module div (
  input  [31:0] In_1,
  input  [31:0] In_2,
  output [31:0] Out
);

  Divider #(.width(32)) divider_1 (.a(In_1), .b(In_2), .out(Out));  // open: upper, rem
endmodule

module rem (
  input  [31:0] In_1,
  input  [31:0] In_2,
  output [31:0] Out
);

  Divider #(.width(32)) divider_1 (.a(In_1), .b(In_2), .rem(Out));  // open: out, upper
endmodule

module mult (
  input  [31:0] In_1,
  input  [31:0] In_2,
  output [31:0] Out
);

  Multiplier #(.width(32)) multiplier_1 (.a(In_1), .b(In_2), .out(Out));  // open: cin, cout
endmodule

module mulh (
  input  [31:0] In_1,
  input  [31:0] In_2,
  output [31:0] Out
);

  Multiplier #(.width(32)) multiplier_1 (.a(In_1), .b(In_2), .cout(Out));  // open: out, cin
endmodule
