// Logisim project cpu.circ as structural Verilog: 8 circuits, main circuit main
module main (
  input  [31:0] INSTRUCTION,
  input  CLOCK,
  output [31:0] FETCH_ADDRESS,
  output [31:0] ra_Value,
  output [31:0] sp_Value,
  output [31:0] t0_Value,
  output [31:0] t1_Value,
  output [31:0] t2_Value,
  output [31:0] s0_Value,
  output [31:0] s1_Value,
  output [31:0] a0_Value
);

  wire ASel, BrEq, BrLt, BrUn, BSel, comparator_1_eq, comparator_1_gt, MEM_p1, MEM_p3, MEM_p9, MEM_p12,
       MEM_p14, MEM_p16, MemRW, MEMSel, or_1_out, PCJump, PCSel, RegWEn;
  wire [1:0] LoadSel, WBSel;
  wire [2:0] ImmSel;
  wire [3:0] ALUSel;
  wire [4:0] instdecoder_1_inst_11_7, instdecoder_1_inst_19_15, instdecoder_1_inst_24_20;
  wire [24:0] instdecoder_1_inst_31_7;
  wire [31:0] alu, imm, instdecoder_1_inst_31_0, InstRegister_q, loadhandler_1_data_out, MEM_p10,
       multiplexer_1_out, multiplexer_2_out, multiplexer_3_out, multiplexer_4_out, multiplexer_5_out,
       multiplexer_6_out, multiplexer_7_out, PC_new_q, PC_old_q, plus_4_out, R1, R2;

  Multiplexer #(.width(32)) multiplexer_1 (
    .in0(PC_new_q), .in1(alu), .out(multiplexer_1_out), .sel(PCJump));  // open: en
  Register #(.width(32)) PC_new (.D(multiplexer_2_out), .Q(PC_new_q), .clk(CLOCK));  // open: en, clr
  Multiplexer #(.width(32)) multiplexer_2 (
    .in0(alu), .in1(plus_4_out), .out(multiplexer_2_out), .sel(PCSel));  // open: en
  Register #(.width(32)) PC_old (.D(multiplexer_1_out), .Q(PC_old_q), .clk(CLOCK));  // open: en, clr
  Register #(.width(32)) InstRegister (.D(multiplexer_3_out), .Q(InstRegister_q), .clk(CLOCK));  // open: en, clr
  Multiplexer #(.width(32)) multiplexer_3 (
    .in0(INSTRUCTION), .in1({32{1'b0}}), .out(multiplexer_3_out), .sel(PCJump));  // open: en
  plus_four plus_4 (.In(PC_new_q), .Out(plus_4_out));
  Shifter #(.width(32), .shift("lr")) shifter_1 (.in(PC_new_q), .\dist (5'b00010), .out(FETCH_ADDRESS));
  InstDecoder instdecoder_1 (
    .Instruction(InstRegister_q), .inst_31_0(instdecoder_1_inst_31_0), .inst_11_7(instdecoder_1_inst_11_7),
    .inst_19_15(instdecoder_1_inst_19_15), .inst_24_20(instdecoder_1_inst_24_20),
    .inst_31_7(instdecoder_1_inst_31_7));
  regfile_main main_1 (
    .Read_Register_1__rs1(instdecoder_1_inst_19_15), .Read_Register_2__rs2(instdecoder_1_inst_24_20),
    .Write_Register__rd(instdecoder_1_inst_11_7), .Write_Data(multiplexer_7_out), .Write_Enable(RegWEn),
    .Clock(CLOCK), .Read_Data_1(R1), .Read_Data_2(R2), .ra_Value(ra_Value), .sp_Value(sp_Value),
    .t0_Value(t0_Value), .t1_Value(t1_Value), .t2_Value(t2_Value), .s0_Value(s0_Value), .s1_Value(s1_Value),
    .a0_Value(a0_Value));  // open: in_7
  ImmGen immgen_1 (.inst_31_7(instdecoder_1_inst_31_7), .ImmSel(ImmSel), .imm_31_0(imm));
  Comparator #(.width(32)) comparator_1 (.a(R2), .b(imm), .gt(comparator_1_gt), .eq(comparator_1_eq));  // open: lt
  BranchComp BranchComp (.A(R1), .B(R2), .BrUn(BrUn), .BrEq(BrEq), .BrLT(BrLt));
  or or_1 (or_1_out, comparator_1_gt, comparator_1_eq);
  Controller controller_1 (
    .PCSel(PCSel), .inst_31_0(instdecoder_1_inst_31_0), .ImmSel(ImmSel), .RegWEn(RegWEn), .BrUn(BrUn),
    .BrEq(BrEq), .BrLt(BrLt), .BSel(BSel), .ASel(ASel), .ALUSel(ALUSel), .MemRW(MemRW), .LoadSel(LoadSel),
    .WBSel(WBSel), .MEMSel(MEMSel), .swgecond(or_1_out), .PCJump(PCJump));
  Multiplexer #(.width(32)) multiplexer_4 (.in0(PC_old_q), .in1(R1), .out(multiplexer_4_out), .sel(ASel));  // open: en
  alu_main main_2 (.Switch(ALUSel), .X(multiplexer_4_out), .Result(alu), .Y(multiplexer_5_out));  // open: Equal
  Multiplexer #(.width(32)) multiplexer_5 (.in0(R2), .in1(imm), .out(multiplexer_5_out), .sel(BSel));  // open: en
  Multiplexer #(.width(32)) multiplexer_6 (.in0(alu), .in1(R1), .out(multiplexer_6_out), .sel(MEMSel));  // open: en
  LoadHandler loadhandler_1 (.Data_In(MEM_p10), .LoadSel(LoadSel), .Data_Out(loadhandler_1_data_out));
  // mem_main MEM: pin names not known; wires that end beside it: MEM_p1, MEM_p1, MEM_p3, multiplexer_6_out, R2, MemRW, MEM_p3, CLOCK, MEM_p9, MEM_p10, MEM_p9, MEM_p12, MEM_p12, MEM_p14, MEM_p14, MEM_p16
  Multiplexer #(.select(2), .width(32)) multiplexer_7 (
    .in0(plus_4_out), .in1(alu), .in2(loadhandler_1_data_out), .in3(imm), .out(multiplexer_7_out), .sel(WBSel));  // open: en

  // Other names for the same wires on the sheet: a0[31:0] = a0_Value; clk = CLOCK; fetch_addr[31:0] = FETCH_ADDRESS;
  //   ra[31:0] = ra_Value; s0[31:0] = s0_Value; s1[31:0] = s1_Value; sp[31:0] = sp_Value; t0[31:0] = t0_Value;
  //   t1[31:0] = t1_Value; t2[31:0] = t2_Value

  // Notes on the sheet:
  //   Output
  //   These are outputs/inputs from run.circ
  //   Inputs
endmodule

module plus_four (
  input  [31:0] In,
  output [31:0] Out
);

  Adder #(.width(32)) adder_1 (.a(In), .b(32'h4), .out(Out));  // open: cin, cout
endmodule

module ImmGen (
  input  [24:0] inst_31_7,
  input  [2:0] ImmSel,
  output [31:0] imm_31_0
);

  wire [31:0] bit_extender_1_out, bit_extender_2_out, bit_extender_3_out, bit_extender_4_out,
       bit_extender_5_out, shifter_1_out;

  assign bit_extender_1_out = {{7{1'b0}}, inst_31_7};  // Bit_Extender bit_extender_1
  Shifter #(.width(32)) shifter_1 (.in(bit_extender_1_out), .\dist (5'b00111), .out(shifter_1_out));
  assign bit_extender_2_out = {{20{shifter_1_out[31]}}, shifter_1_out[31:20]};  // Bit_Extender bit_extender_2
  assign bit_extender_3_out = {{20{shifter_1_out[31]}}, {shifter_1_out[31:25], shifter_1_out[11:7]}};  // Bit_Extender bit_extender_3
  assign bit_extender_4_out = {{19{shifter_1_out[31]}}, {shifter_1_out[31], shifter_1_out[7], shifter_1_out[30:25], shifter_1_out[11:8], 1'b0}};  // Bit_Extender bit_extender_4
  assign bit_extender_5_out = {{11{shifter_1_out[31]}}, {shifter_1_out[31], shifter_1_out[19:12], shifter_1_out[20], shifter_1_out[30:21], 1'b0}};  // Bit_Extender bit_extender_5
  Multiplexer #(.select(3), .width(32)) multiplexer_1 (
    .in0(bit_extender_2_out), .in1(bit_extender_3_out), .in2(bit_extender_4_out),
    .in3({shifter_1_out[31:12], {12{1'b0}}}), .in4(bit_extender_5_out), .out(imm_31_0), .sel(ImmSel));  // open: in5, in6, in7, en

  // Notes on the sheet:
  //   I-Type
  //   S-Type
  //   B-Type
  //   U-Type
  //   J-Type
  //   0 = I-Type, 1 = S-Type, 2 = B-Type, 3 = U-Type, 4 = J-Type
endmodule

module BranchComp (
  input  [31:0] A,
  input  [31:0] B,
  input  BrUn,
  output BrEq,
  output BrLT
);

  wire comparator_1_eq, comparator_1_lt, comparator_2_eq, comparator_2_lt;

  Comparator #(.width(32), .mode("unsigned")) comparator_1 (
    .a(A), .b(B), .eq(comparator_1_eq), .lt(comparator_1_lt));  // open: gt
  Comparator #(.width(32)) comparator_2 (.a(A), .b(B), .eq(comparator_2_eq), .lt(comparator_2_lt));  // open: gt
  Multiplexer multiplexer_1 (.in0(comparator_2_eq), .in1(comparator_1_eq), .out(BrEq), .sel(BrUn));  // open: en
  Multiplexer multiplexer_2 (.in0(comparator_2_lt), .in1(comparator_1_lt), .out(BrLT), .sel(BrUn));  // open: en
endmodule

module Controller (
  input  BrEq,
  input  BrLt,
  input  [31:0] inst_31_0,
  input  swgecond,
  output PCSel,
  output [2:0] ImmSel,
  output RegWEn,
  output BrUn,
  output BSel,
  output ASel,
  output [3:0] ALUSel,
  output MemRW,
  output [1:0] LoadSel,
  output [1:0] WBSel,
  output MEMSel,
  output PCJump
);

  wire add, addi, \and , and_1_out, and_3_out, and_4_out, and_5_out, andi, B_out, beq, blt, comparator_1_eq,
       div, I_out, J_out, jal, jalr, lb, lh, lui, lw, mul, mulh, not_5_out, not_6_out, \or , or_1_out,
       or_2_out, or_4_out, or_5_out, or_6_out, or_7_out, ori, rem, S_out, sll, slli, slt, slti, srl, srli,
       sub, sw, swge, U_out, \xor , xori;

  InstIdentifier instidentifier_1 (
    .opcode(inst_31_0[6:0]), .funct3(inst_31_0[14:12]), .funct7(inst_31_0[31:25]), .add(add), .mul(mul),
    .sub(sub), .sll(sll), .mulh(mulh), .slt(slt), .\xor (\xor ), .div(div), .srl(srl), .\or (\or ),
    .rem(rem), .\and (\and ), .lb(lb), .lh(lh), .lw(lw), .addi(addi), .slli(slli), .slti(slti), .xori(xori),
    .srli(srli), .ori(ori), .andi(andi), .sw(sw), .swge(swge), .beq(beq), .blt(blt), .bltu(BrUn), .lui(lui),
    .jal(jal), .jalr(jalr));
  or or_1 (or_1_out, sw, swge, beq, blt, BrUn);
  not not_1 (RegWEn, or_1_out);
  or or_2 (or_2_out, beq, blt, BrUn, jal);
  Comparator #(.width(7)) comparator_1 (.a(inst_31_0[6:0]), .b(7'b0110011), .eq(comparator_1_eq));  // open: gt, lt
  or or_3 (MemRW, sw, swge);
  and and_1 (and_1_out, beq, BrEq);
  assign ImmSel = I_out ? 3'b000 : 3'bz;  // Controlled_Buffer controlled_buffer_1
  or I (I_out, lb, lh, lw, addi, slli, slti, xori, srli, ori, andi, jalr);
  or S (S_out, sw, swge);
  or B (B_out, beq, blt, BrUn);
  or U (U_out, lui, 1'b0);
  or J (J_out, jal, 1'b0);
  not not_2 (ASel, or_2_out);
  not not_3 (BSel, comparator_1_eq);
  not not_4 (PCSel, or_4_out);
  or or_4 (or_4_out, and_1_out, blt, BrUn, jalr, jal);
  assign ImmSel = S_out ? 3'b001 : 3'bz;  // Controlled_Buffer controlled_buffer_2
  assign ImmSel = B_out ? 3'b010 : 3'bz;  // Controlled_Buffer controlled_buffer_3
  assign ImmSel = U_out ? 3'b011 : 3'bz;  // Controlled_Buffer controlled_buffer_4
  assign ImmSel = J_out ? 3'b100 : 3'bz;  // Controlled_Buffer controlled_buffer_5
  or or_5 (or_5_out, jal, jalr, lw, lui);
  or or_6 (or_6_out, mulh, mul, rem, div, slt, sll, srl, \xor , \or );
  assign WBSel = not_5_out ? 2'b01 : 2'bz;  // Controlled_Buffer controlled_buffer_6
  not not_5 (not_5_out, or_5_out);
  assign WBSel = lui ? 2'b11 : 2'bz;  // Controlled_Buffer controlled_buffer_7
  assign WBSel = lw ? 2'b10 : 2'bz;  // Controlled_Buffer controlled_buffer_8
  assign WBSel = or_7_out ? 2'b00 : 2'bz;  // Controlled_Buffer controlled_buffer_9
  or or_7 (or_7_out, jalr, jal);
  assign ALUSel = not_6_out ? 4'b0000 : 4'bz;  // Controlled_Buffer controlled_buffer_10
  not not_6 (not_6_out, or_6_out);
  assign ALUSel = \and  ? 4'b0001 : 4'bz;  // Controlled_Buffer controlled_buffer_11
  assign ALUSel = \or  ? 4'b0010 : 4'bz;  // Controlled_Buffer controlled_buffer_12
  assign ALUSel = \xor  ? 4'b0011 : 4'bz;  // Controlled_Buffer controlled_buffer_13
  assign ALUSel = srl ? 4'b0100 : 4'bz;  // Controlled_Buffer controlled_buffer_14
  assign ALUSel = sll ? 4'b0110 : 4'bz;  // Controlled_Buffer controlled_buffer_15
  assign ALUSel = slt ? 4'b0111 : 4'bz;  // Controlled_Buffer controlled_buffer_16
  assign ALUSel = div ? 4'b1000 : 4'bz;  // Controlled_Buffer controlled_buffer_17
  assign ALUSel = rem ? 4'b1001 : 4'bz;  // Controlled_Buffer controlled_buffer_18
  assign ALUSel = mul ? 4'b1010 : 4'bz;  // Controlled_Buffer controlled_buffer_19
  assign ALUSel = mulh ? 4'b1011 : 4'bz;  // Controlled_Buffer controlled_buffer_20
  and and_2 (MEMSel, swge, swgecond);
  assign LoadSel = lw ? 2'b00 : 2'bz;  // Controlled_Buffer controlled_buffer_21
  assign LoadSel = lb ? 2'b01 : 2'bz;  // Controlled_Buffer controlled_buffer_22
  assign LoadSel = lh ? 2'b10 : 2'bz;  // Controlled_Buffer controlled_buffer_23
  and and_3 (and_3_out, beq, BrEq);
  and and_4 (and_4_out, blt, BrLt);
  and and_5 (and_5_out, BrLt, BrUn);
  or or_8 (PCJump, and_3_out, and_4_out, and_5_out, jal, jalr);

  // Other names for the same wires on the sheet: bltu = BrUn; inst[31:0] = inst_31_0; opcode[6:0] = inst_31_0[6:0];
  //   funct3[2:0] = inst_31_0[14:12]; funct7[6:0] = inst_31_0[31:25]
endmodule

module InstDecoder (
  input  [31:0] Instruction,
  output [4:0] inst_11_7,
  output [4:0] inst_19_15,
  output [4:0] inst_24_20,
  output [24:0] inst_31_7,
  output [31:0] inst_31_0
);


  assign inst_11_7 = Instruction[11:7];
  assign inst_19_15 = Instruction[19:15];
  assign inst_24_20 = Instruction[24:20];
  assign inst_31_0 = Instruction;
  assign inst_31_7 = Instruction[31:7];
endmodule

module InstIdentifier (
  input  [6:0] opcode,
  input  [2:0] funct3,
  input  [6:0] funct7,
  output add,
  output mul,
  output sub,
  output sll,
  output mulh,
  output slt,
  output \xor ,
  output div,
  output srl,
  output \or ,
  output rem,
  output \and ,
  output lb,
  output lh,
  output lw,
  output addi,
  output slli,
  output slti,
  output xori,
  output srli,
  output ori,
  output andi,
  output sw,
  output swge,
  output beq,
  output blt,
  output bltu,
  output lui,
  output jal,
  output jalr
);

  wire comparator_1_eq, comparator_2_eq, comparator_3_eq, comparator_4_eq, comparator_5_eq, comparator_6_eq,
       comparator_7_eq, comparator_8_eq, comparator_9_eq, comparator_10_eq, comparator_11_eq,
       comparator_12_eq, comparator_13_eq, comparator_14_eq, comparator_15_eq, comparator_16_eq,
       comparator_17_eq, comparator_18_eq;

  Comparator #(.width(7), .mode("unsigned")) comparator_1 (
    .a(opcode), .b(7'b0110011), .eq(comparator_1_eq));  // open: gt, lt
  Comparator #(.width(7), .mode("unsigned")) comparator_2 (
    .a(opcode), .b(7'b0000011), .eq(comparator_2_eq));  // open: gt, lt
  Comparator #(.width(7), .mode("unsigned")) comparator_3 (
    .a(opcode), .b(7'b0010011), .eq(comparator_3_eq));  // open: gt, lt
  Comparator #(.width(7), .mode("unsigned")) comparator_4 (
    .a(opcode), .b(7'b0100011), .eq(comparator_4_eq));  // open: gt, lt
  Comparator #(.width(7), .mode("unsigned")) comparator_5 (
    .a(opcode), .b(7'b1100011), .eq(comparator_5_eq));  // open: gt, lt
  Comparator #(.width(7), .mode("unsigned")) comparator_6 (
    .a(opcode), .b(7'b0110111), .eq(comparator_6_eq));  // open: gt, lt
  Comparator #(.width(7), .mode("unsigned")) comparator_7 (
    .a(opcode), .b(7'b1101111), .eq(comparator_7_eq));  // open: gt, lt
  Comparator #(.width(7), .mode("unsigned")) comparator_8 (
    .a(opcode), .b(7'b1100111), .eq(comparator_8_eq));  // open: gt, lt
  Comparator #(.width(3), .mode("unsigned")) comparator_9 (
    .a(funct3), .b(3'b000), .eq(comparator_9_eq));  // open: gt, lt
  Comparator #(.width(3), .mode("unsigned")) comparator_10 (
    .a(funct3), .b(3'b001), .eq(comparator_10_eq));  // open: gt, lt
  Comparator #(.width(3), .mode("unsigned")) comparator_11 (
    .a(funct3), .b(3'b010), .eq(comparator_11_eq));  // open: gt, lt
  Comparator #(.width(3), .mode("unsigned")) comparator_12 (
    .a(funct3), .b(3'b100), .eq(comparator_12_eq));  // open: gt, lt
  Comparator #(.width(3), .mode("unsigned")) comparator_13 (
    .a(funct3), .b(3'b101), .eq(comparator_13_eq));  // open: gt, lt
  Comparator #(.width(3), .mode("unsigned")) comparator_14 (
    .a(funct3), .b(3'b110), .eq(comparator_14_eq));  // open: gt, lt
  Comparator #(.width(3), .mode("unsigned")) comparator_15 (
    .a(funct3), .b(3'b111), .eq(comparator_15_eq));  // open: gt, lt
  Comparator #(.width(7), .mode("unsigned")) comparator_16 (
    .a(funct7), .b({7{1'b0}}), .eq(comparator_16_eq));  // open: gt, lt
  Comparator #(.width(7), .mode("unsigned")) comparator_17 (
    .a(funct7), .b(7'b0000001), .eq(comparator_17_eq));  // open: gt, lt
  Comparator #(.width(7), .mode("unsigned")) comparator_18 (
    .a(funct7), .b(7'b0100000), .eq(comparator_18_eq));  // open: gt, lt
  and and_1 (add, comparator_1_eq, comparator_9_eq, comparator_16_eq);
  and and_2 (mul, comparator_1_eq, comparator_9_eq, comparator_17_eq);
  and and_3 (sub, comparator_1_eq, comparator_9_eq, comparator_18_eq);
  and and_4 (sll, comparator_1_eq, comparator_10_eq, comparator_16_eq);
  and and_5 (mulh, comparator_1_eq, comparator_10_eq, comparator_17_eq);
  and and_6 (slt, comparator_1_eq, comparator_11_eq, comparator_16_eq);
  and and_7 (\xor , comparator_1_eq, comparator_12_eq, comparator_16_eq);
  and and_8 (div, comparator_1_eq, comparator_12_eq, comparator_17_eq);
  and and_9 (srl, comparator_1_eq, comparator_13_eq, comparator_16_eq);
  and and_10 (\or , comparator_1_eq, comparator_14_eq, comparator_16_eq);
  and and_11 (rem, comparator_1_eq, comparator_14_eq, comparator_17_eq);
  and and_12 (\and , comparator_1_eq, comparator_15_eq, comparator_16_eq);
  and and_13 (lb, comparator_2_eq, comparator_9_eq);
  and and_14 (lh, comparator_2_eq, comparator_10_eq);
  and and_15 (lw, comparator_2_eq, comparator_11_eq);
  and and_16 (addi, comparator_3_eq, comparator_9_eq);
  and and_17 (slli, comparator_3_eq, comparator_10_eq, comparator_16_eq);
  and and_18 (slti, comparator_3_eq, comparator_11_eq);
  and and_19 (xori, comparator_3_eq, comparator_12_eq);
  and and_20 (srli, comparator_3_eq, comparator_13_eq, comparator_16_eq);
  and and_21 (ori, comparator_3_eq, comparator_14_eq);
  and and_22 (andi, comparator_3_eq, comparator_15_eq);
  and and_23 (sw, comparator_4_eq, comparator_11_eq);
  and and_24 (swge, comparator_4_eq, comparator_15_eq);
  and and_25 (beq, comparator_5_eq, comparator_9_eq);
  and and_26 (blt, comparator_5_eq, comparator_12_eq);
  and and_27 (bltu, comparator_5_eq, comparator_14_eq);
  buf and_28 (lui, comparator_6_eq);  // AND_Gate
  buf and_29 (jal, comparator_7_eq);  // AND_Gate
  and and_30 (jalr, comparator_8_eq, comparator_9_eq);
endmodule

module LoadHandler (
  input  [31:0] Data_In,
  input  [1:0] LoadSel,
  output [31:0] Data_Out
);

  Multiplexer #(.select(2), .width(32)) multiplexer_1 (
    .in0(Data_In), .in1({{24{1'b0}}, Data_In[7:0]}), .in2({{16{1'b0}}, Data_In[15:0]}), .out(Data_Out),
    .sel(LoadSel));  // open: in3, en

  // Notes on the sheet:
  //   lw
  //   lh
  //   lb
endmodule
