// Logisim project regfile.circ as structural Verilog: 1 circuit, main circuit main
module main (
  input  [4:0] Read_Register_1__rs1,
  input  [4:0] Read_Register_2__rs2,
  input  [4:0] Write_Register__rd,
  input  [31:0] Write_Data,
  input  Write_Enable,
  input  Clock,
  input  in_7,
  output [31:0] ra_Value,
  output [31:0] sp_Value,
  output [31:0] t0_Value,
  output [31:0] t1_Value,
  output [31:0] t2_Value,
  output [31:0] s0_Value,
  output [31:0] s1_Value,
  output [31:0] a0_Value,
  output [31:0] Read_Data_1,
  output [31:0] Read_Data_2
);

  wire and_1_out, and_2_out, and_3_out, and_4_out, and_5_out, and_6_out, and_7_out, and_8_out, and_9_out,
       and_10_out, write_a0, write_a1, write_ra, write_s0, write_s1, write_sp, write_t0, write_t1, write_t2,
       write_x0, write_zero;
  wire [31:0] a1_val, multiplexer_1_out, multiplexer_2_out, multiplexer_3_out, multiplexer_4_out,
       multiplexer_5_out, multiplexer_6_out, multiplexer_7_out, multiplexer_8_out, multiplexer_9_out,
       multiplexer_10_out, x0_val;

  Demultiplexer #(.select(5)) demultiplexer_1 (
    .out0(write_zero), .out1(write_ra), .out2(write_sp), .out5(write_t0), .out6(write_t1), .out7(write_t2),
    .out8(write_s0), .out9(write_s1), .out10(write_a0), .out11(write_a1), .in(in_7), .sel(Write_Register__rd));  // open: out3, out4, out12, out13, out14, out15, out16, out17, out18, out19, out20, out21, out22, out23, out24, out25, out26, out27, out28, out29, out30, out31, en
  and and_1 (and_1_out, Write_Enable, write_x0);
  and and_2 (and_2_out, Write_Enable, write_sp);
  and and_3 (and_3_out, Write_Enable, write_t1);
  and and_4 (and_4_out, Write_Enable, write_s0);
  and and_5 (and_5_out, Write_Enable, write_a0);
  Multiplexer #(.width(32)) multiplexer_1 (
    .in0(x0_val), .in1(x0_val), .out(multiplexer_1_out), .sel(and_1_out));  // open: en
  Register #(.width(32)) x0 (.D(multiplexer_1_out), .Q(x0_val), .clk(Clock));  // open: en, clr
  Register #(.width(32)) sp (.D(multiplexer_2_out), .Q(sp_Value), .clk(Clock));  // open: en, clr
  Multiplexer #(.width(32)) multiplexer_2 (
    .in0(sp_Value), .in1(Write_Data), .out(multiplexer_2_out), .sel(and_2_out));  // open: en
  Multiplexer #(.width(32)) multiplexer_3 (
    .in0(t1_Value), .in1(Write_Data), .out(multiplexer_3_out), .sel(and_3_out));  // open: en
  Register #(.width(32)) t1 (.D(multiplexer_3_out), .Q(t1_Value), .clk(Clock));  // open: en, clr
  Register #(.width(32)) s0 (.D(multiplexer_4_out), .Q(s0_Value), .clk(Clock));  // open: en, clr
  Multiplexer #(.width(32)) multiplexer_4 (
    .in0(s0_Value), .in1(Write_Data), .out(multiplexer_4_out), .sel(and_4_out));  // open: en
  Multiplexer #(.width(32)) multiplexer_5 (
    .in0(a0_Value), .in1(Write_Data), .out(multiplexer_5_out), .sel(and_5_out));  // open: en
  Register #(.width(32)) a0 (.D(multiplexer_5_out), .Q(a0_Value), .clk(Clock));  // open: en, clr
  and and_6 (and_6_out, Write_Enable, write_ra);
  and and_7 (and_7_out, Write_Enable, write_t0);
  and and_8 (and_8_out, Write_Enable, write_t2);
  and and_9 (and_9_out, Write_Enable, write_s1);
  and and_10 (and_10_out, Write_Enable, write_a1);
  Multiplexer #(.width(32)) multiplexer_6 (
    .in0(ra_Value), .in1(Write_Data), .out(multiplexer_6_out), .sel(and_6_out));  // open: en
  Register #(.width(32)) ra (.D(multiplexer_6_out), .Q(ra_Value), .clk(Clock));  // open: en, clr
  Register #(.width(32)) t0 (.D(multiplexer_7_out), .Q(t0_Value), .clk(Clock));  // open: en, clr
  Multiplexer #(.width(32)) multiplexer_7 (
    .in0(t0_Value), .in1(Write_Data), .out(multiplexer_7_out), .sel(and_7_out));  // open: en
  Register #(.width(32)) t2 (.D(multiplexer_8_out), .Q(t2_Value), .clk(Clock));  // open: en, clr
  Multiplexer #(.width(32)) multiplexer_8 (
    .in0(t2_Value), .in1(Write_Data), .out(multiplexer_8_out), .sel(and_8_out));  // open: en
  Multiplexer #(.width(32)) multiplexer_9 (
    .in0(s1_Value), .in1(Write_Data), .out(multiplexer_9_out), .sel(and_9_out));  // open: en
  Register #(.width(32)) s1 (.D(multiplexer_9_out), .Q(s1_Value), .clk(Clock));  // open: en, clr
  Multiplexer #(.width(32)) multiplexer_10 (
    .in0(a1_val), .in1(Write_Data), .out(multiplexer_10_out), .sel(and_10_out));  // open: en
  Register #(.width(32)) a1 (.D(multiplexer_10_out), .Q(a1_val), .clk(Clock));  // open: en, clr
  Multiplexer #(.select(5), .width(32)) multiplexer_11 (
    .in0(x0_val), .in1(ra_Value), .in2(sp_Value), .in5(t0_Value), .in6(t1_Value), .in7(t2_Value),
    .in8(s0_Value), .in9(s1_Value), .in10(a0_Value), .in11(a1_val), .out(Read_Data_1),
    .sel(Read_Register_1__rs1));  // open: in3, in4, in12, in13, in14, in15, in16, in17, in18, in19, in20, in21, in22, in23, in24, in25, in26, in27, in28, in29, in30, in31, en
  Multiplexer #(.select(5), .width(32)) multiplexer_12 (
    .in0(x0_val), .in1(ra_Value), .in2(sp_Value), .in5(t0_Value), .in6(t1_Value), .in7(t2_Value),
    .in8(s0_Value), .in9(s1_Value), .in10(a0_Value), .in11(a1_val), .out(Read_Data_2),
    .sel(Read_Register_2__rs2));  // open: in3, in4, in12, in13, in14, in15, in16, in17, in18, in19, in20, in21, in22, in23, in24, in25, in26, in27, in28, in29, in30, in31, en

  // Other names for the same wires on the sheet: a0_val[31:0] = a0_Value; clk = Clock; ra_val[31:0] = ra_Value;
  //   read_data1[31:0] = Read_Data_1; read_data2[31:0] = Read_Data_2; read_reg1[4:0] = Read_Register_1__rs1;
  //   read_reg2[4:0] = Read_Register_2__rs2; s0_val[31:0] = s0_Value; s1_val[31:0] = s1_Value;
  //   sp_val[31:0] = sp_Value; t0_val[31:0] = t0_Value; t1_val[31:0] = t1_Value; t2_val[31:0] = t2_Value;
  //   write_en = Write_Enable; write_reg[4:0] = Write_Register__rd

  // Notes on the sheet:
  //   INPUTS to your circuit
  //   These are DEBUG/TEST outputs from your circuit.
  //   DON'T CHANGE THE LOCATIONS OF THE INPUTS AND OUTPUTS!
  //   OUTPUTS from your circuit
endmodule
